# Fritzing sketch OBSbasic (saved by Fritzing 0.7.12b)
breadboards: 1

parts:
  QRD114 = mystery part, 4 pins [chip_label=QRD114]
  R5 = Resistor [tolerance=±10% resistance=100 package=THT]
  R6 = Resistor [tolerance=±10% resistance=100 package=THT]
  R4 = Resistor [tolerance=±10% resistance=4.7k package=THT]
  Arduino1 = Arduino

nets (from the breadboard view):
  N1: QRD114.pin1, Arduino1.D8
  N2: QRD114.pin2, R4.Pin_0, Arduino1.A0
  N3: QRD114.pin3, R6.Pin_0
  N4: QRD114.pin4, R4.Pin_1, Arduino1.GND
  N5: R5.Pin_0, R6.Pin_1
  N6: R5.Pin_1, Arduino1.D9
